# Fritzing sketch ElectricalDiagram (saved by Fritzing 1.0.2b)
breadboards: 1

parts:
  Teensy1 = Teensy 4.1
  CUI-enc1 = AMT103  # not connected
  CUI-enc2 = AMT103  # not connected
  CUI-enc3 = AMT103  # not connected
  CUI-enc4 = AMT103  # not connected
  CUI-enc5 = AMT103  # not connected
  CUI-enc6 = AMT103  # not connected
  S1 = D2F-FL Omron Snap Action Limit Switch with Level  # not connected
  S2 = D2F-FL Omron Snap Action Limit Switch with Level  # not connected
  S3 = D2F-FL Omron Snap Action Limit Switch with Level  # not connected
  S4 = D2F-FL Omron Snap Action Limit Switch with Level  # not connected
  S5 = D2F-FL Omron Snap Action Limit Switch with Level  # not connected
  S6 = D2F-FL Omron Snap Action Limit Switch with Level  # not connected
  M1 = Stepper Motor - Bipolar  # not connected
  M2 = Stepper Motor - Bipolar  # not connected
  M3 = Stepper Motor - Bipolar  # not connected
  M4 = Stepper Motor - Bipolar  # not connected
  M5 = Stepper Motor - Bipolar  # not connected
  M6 = Stepper Motor - Bipolar  # not connected
  Part1 = EasyDriver_v44  # not connected
  Part2 = EasyDriver_v44  # not connected
  Part3 = EasyDriver_v44  # not connected
  Part4 = EasyDriver_v44  # not connected
  Part5 = EasyDriver_v44  # not connected
  Part6 = EasyDriver_v44  # not connected
  EVB-LAN9252-SPI1 = EVB-LAN9252-SPI [part_number=EVB-LAN9252-SPI]  # not connected

nets:
  N1: Teensy1.GND, Teensy1.GND2#55

custom parts:
  Teensy 4.1: The Teensy is a complete USB-based microcontoller development system, in a very small footprint, capable of implementing many types of projects. All programming is done via the USB port. No special programmer is needed, only a standard micro-USB cable and a PC or Macintosh with a USB port.
  D2F-FL Omron Snap Action Limit Switch with Level: Snap action switch with stainless steel lever.
